// Logisim project minikit_logisim.circ as structural Verilog: 2 circuits, main circuit main
module main (
  input  x,
  input  A,
  input  F,
  input  y,
  input  z,
  input  B,
  input  in_7,
  input  in_8,
  input  in_9,
  input  x_2,
  input  y_2,
  input  in_12,
  input  z_2,
  input  in_14,
  input  in_15,
  input  in_16,
  input  in_17,
  input  in_18,
  input  in_19,
  input  in_20,
  input  in_21,
  input  in_22,
  input  in_23,
  input  in_24,
  input  in_25,
  input  in_26,
  input  in_27,
  input  in_28,
  input  in_29,
  input  in_30,
  input  in_31,
  input  in_32,
  input  in_33,
  input  in_34,
  input  in_35,
  input  in_36,
  input  in_37,
  input  in_38,
  input  in_39,
  input  in_40,
  input  in_41,
  input  in_42,
  input  a_2,
  input  Carry_in,
  input  b_2,
  input  c,
  input  d,
  input  a_3,
  input  b_3,
  input  Carry_in_2,
  input  D0,
  input  A0,
  input  A1,
  input  D1,
  input  D2,
  input  D3,
  input  [1:0] A_4,
  input  s1,
  input  s0,
  output cout,
  output s,
  output Q0,
  output Q0_2,
  output Q2,
  output Q1,
  output Q1_2,
  output Q3,
  output Q2_2,
  output Q3_2
);

  wire AND_2_out, AND_3_out, AND_4_out, AND_5_out, AND_6_out, AND_7_out, AND_8_out, AND_9_out, AND_10_out,
       AND_11_out, AND_12_out, AND_13_out, AND_14_out, and_15_out, and_16_out, and_17_out, and_18_out,
       and_19_out, and_20_out, and_25_out, and_26_out, and_27_out, and_28_out, and_29_out, and_30_out,
       and_31_out, AND_out, NAND_2_out, NAND_3_out, NAND_4_out, NAND_5_out, NAND_6_out, NAND_7_out,
       NAND_8_out, NAND_9_out, NAND_10_out, NAND_11_out, NAND_12_out, NAND_13_out, NAND_14_out, NAND_15_out,
       nand_16_out, NAND_out, nor_2_out, NOR_out, not_1_out, not_2_out, not_3_out, not_4_out, not_5_out,
       not_6_out, not_7_out, not_8_out, not_9_out, not_10_out, not_11_out, not_12_out, not_13_out,
       not_14_out, not_15_out, not_16_out, not_17_out, not_18_out, not_19_out, not_20_out, not_21_out,
       not_22_out, not_23_out, not_24_out, not_25_out, not_26_out, not_27_out, not_28_out, not_29_out,
       OR_2_out, OR_3_out, or_4_out, OR_5_out, OR_6_out, OR_7_out, or_8_out, or_10_out, or_11_out, OR_out,
       xnor_1_out, xnor_2_out, XOR_2_out, XOR_3_out, XOR_4_out, XOR_5_out, xor_6_out, xor_7_out, XOR_out;

  LED led_1 (.in(1'b0));
  LED led_2 (.in(1'b1));
  not not_1 (not_1_out, in_8);
  not not_2 (not_2_out, in_9);
  not not_3 (not_3_out, in_15);
  not not_4 (not_4_out, in_16);
  not not_5 (not_5_out, in_25);
  not not_6 (not_6_out, in_26);
  not not_7 (not_7_out, in_31);
  not not_8 (not_8_out, in_32);
  not not_9 (not_9_out, in_38);
  not not_10 (not_10_out, in_37);
  not not_11 (not_11_out, s1);
  and AND (AND_out, A, B);
  or OR (OR_out, not_1_out, not_2_out);
  nand NAND (NAND_out, in_12, in_14);
  or OR_2 (OR_2_out, not_3_out, not_4_out);
  or OR_3 (OR_3_out, in_21, in_23);
  and AND_2 (AND_2_out, not_5_out, not_6_out);
  nor NOR (NOR_out, in_27, in_29);
  and AND_3 (AND_3_out, not_7_out, not_8_out);
  xor XOR (XOR_out, in_33, in_35);
  and AND_4 (AND_4_out, in_37, not_9_out);
  or or_4 (or_4_out, AND_4_out, AND_5_out);
  and AND_5 (AND_5_out, not_10_out, in_38);
  not not_12 (not_12_out, in_39);
  nand NAND_2 (NAND_2_out, in_40, in_40);
  LED led_3 (.in(AND_out));
  not not_13 (not_13_out, OR_out);
  LED led_4 (.in(not_13_out));
  LED led_5 (.in(NAND_out));
  LED led_6 (.in(OR_2_out));
  LED led_7 (.in(OR_3_out));
  LED led_8 (.in(not_14_out));
  not not_14 (not_14_out, AND_2_out);
  LED led_9 (.in(NOR_out));
  LED led_10 (.in(AND_3_out));
  LED led_11 (.in(XOR_out));
  LED led_12 (.in(or_4_out));
  LED led_13 (.in(not_12_out));
  LED led_14 (.in(NAND_2_out));
  xor XOR_2 (XOR_2_out, in_41, in_42);
  xor XOR_3 (XOR_3_out, a_3, b_3);
  and AND_6 (AND_6_out, D0, not_11_out, not_15_out);
  not not_15 (not_15_out, s0);
  and AND_7 (AND_7_out, D1, not_11_out, s0);
  and AND_8 (AND_8_out, D2, s1, not_16_out);
  not not_16 (not_16_out, s0);
  and AND_9 (AND_9_out, D3, s1, s0);
  nand NAND_3 (NAND_3_out, F, in_7);
  nand NAND_4 (NAND_4_out, in_28, in_28);
  nand NAND_5 (NAND_5_out, in_30, in_30);
  nand NAND_6 (NAND_6_out, in_34, in_36);
  nand NAND_7 (NAND_7_out, NAND_3_out, NAND_3_out);
  LED led_15 (.in(NAND_7_out));
  nand NAND_8 (NAND_8_out, in_22, in_22);
  nand NAND_9 (NAND_9_out, NAND_8_out, NAND_10_out);
  nand NAND_10 (NAND_10_out, in_24, in_24);
  nand NAND_11 (NAND_11_out, NAND_4_out, NAND_5_out);
  nand NAND_12 (NAND_12_out, in_34, NAND_6_out);
  nand NAND_13 (NAND_13_out, NAND_6_out, in_36);
  xor XOR_4 (XOR_4_out, XOR_2_out, Carry_in);
  and AND_10 (AND_10_out, XOR_2_out, Carry_in);
  and AND_11 (AND_11_out, in_41, in_42);
  xor XOR_5 (XOR_5_out, XOR_3_out, Carry_in_2);
  and AND_12 (AND_12_out, b_3, a_3);
  and AND_13 (AND_13_out, b_3, Carry_in_2);
  and AND_14 (AND_14_out, a_3, Carry_in_2);
  LED led_16 (.in(OR_5_out));
  or OR_5 (OR_5_out, AND_6_out, AND_7_out, AND_8_out, AND_9_out);
  LED led_17 (.in(NAND_9_out));
  LED led_18 (.in(NAND_14_out));
  nand NAND_14 (NAND_14_out, NAND_11_out, NAND_11_out);
  nand NAND_15 (NAND_15_out, NAND_12_out, NAND_13_out);
  LED led_19 (.in(NAND_15_out));
  LED led_20 (.in(XOR_4_out));
  LED led_21 (.in(OR_6_out));
  or OR_6 (OR_6_out, AND_10_out, AND_11_out);
  LED led_22 (.in(XOR_5_out));
  LED led_23 (.in(OR_7_out));
  or OR_7 (OR_7_out, AND_12_out, AND_13_out, AND_14_out);
  not not_17 (not_17_out, A0);
  not not_18 (not_18_out, A1);
  and and_15 (and_15_out, a_2, b_2);
  and and_16 (and_16_out, a_2, c);
  and and_17 (and_17_out, b_2, c);
  and and_18 (and_18_out, a_2, d);
  and and_19 (and_19_out, b_2, d);
  and and_20 (and_20_out, c, d);
  xor odd_parity_1 (s, a_2, b_2, c, d);
  and AND_21 (Q0_2, not_17_out, not_18_out);
  and AND_22 (Q1, A0, not_18_out);
  and AND_23 (Q2_2, A1, not_17_out);
  and AND_24 (Q3_2, A1, A0);
  not not_19 (not_19_out, x);
  not not_20 (not_20_out, y);
  not not_21 (not_21_out, z);
  not not_22 (not_22_out, x_2);
  not not_23 (not_23_out, y_2);
  and and_25 (and_25_out, not_19_out, not_20_out, not_21_out);
  not not_24 (not_24_out, x);
  and and_26 (and_26_out, not_24_out, z, not_25_out);
  not not_25 (not_25_out, y);
  and and_27 (and_27_out, not_22_out, y_2);
  or or_8 (or_8_out, x_2, not_23_out, z_2);
  and and_28 (and_28_out, in_17, in_18);
  not not_26 (not_26_out, in_19);
  and and_29 (and_29_out, in_19, not_27_out);
  not not_27 (not_27_out, in_20);
  or or_9 (cout, and_15_out, and_16_out, and_17_out, and_18_out, and_19_out, and_20_out);
  Decoder #(.select(2), .enable("false")) decoder_1 (.out0(Q0), .out1(Q2), .out2(Q1_2), .out3(Q3), .sel(A_4));
  or or_10 (or_10_out, and_25_out, and_26_out);
  not not_28 (not_28_out, and_27_out);
  not not_29 (not_29_out, or_8_out);
  nor nor_2 (nor_2_out, in_17, in_19, in_20);
  xor xor_6 (xor_6_out, in_19, in_20);
  xnor xnor_1 (xnor_1_out, in_17, in_18);
  LED led_24 (.in(or_10_out));
  xnor xnor_2 (xnor_2_out, not_28_out, not_29_out);
  and and_30 (and_30_out, and_28_out, or_11_out);
  or or_11 (or_11_out, not_26_out, xor_6_out);
  and and_31 (and_31_out, xnor_1_out, and_29_out);
  LED led_25 (.in(nand_16_out));
  nand nand_16 (nand_16_out, xnor_2_out, z_2);
  ExactlyOne xor_7 (.out(xor_7_out), .in0(nor_2_out), .in1(and_30_out), .in2(and_31_out));
  LED led_26 (.in(xor_7_out));

  // Notes on the sheet:
  //   Porta Conectivo de Sheffer (NAND)
  //   Não (NOT)
  //   Porta E (AND)
  //   Porta OU (OR)
  //   Porta  (NOR)
  //   Porta XOU (XOR)
  //   NOT
  //   Somador Completo de 3 bits
  //   Multiplexador de 4 entradas
  //   A.B=F
  //   A+B=F
  //   A=F
  //   A+B=F
  //   A⊕B=F
  //   input
  //   A
  //   0
  //   0
  //   1
  //   1
  //   A
  //   0
  //   0
  //   1
  //   1
  //   input
  //   A
  //   0
  //   0
  //   1
  //   1
  //   Y
  //   B
  //   0
  //   1
  //   0
  //   1
  //   A.B=F
  //   input
  //   B
  //   0
  //   1
  //   0
  //   1
  //   B
  //   0
  //   1
  //   0
  //   1
  //   input
  //   A
  //   B
  //   0
  //   0
  //   1
  //   0
  //   0
  //   1
  //   1
  //   1
  //   input
  //   A
  //   B
  //   0
  //   0
  //   1
  //   0
  //   0
  //   1
  //   1
  //   1
  //   s
  //   carry out
  //   output
  //   F
  //   0
  //   0
  //   0
  //   1
  //   output
  //   F
  //   1
  //   1
  //   1
  //   0
  //   output
  //   F
  //   0
  //   1
  //   1
  //   1
  //   output
  //   F
  //   1
  //   0
  //   0
  //   0
  //   output
  //   F
  //   0
  //   1
  //   1
  //   0
  //   Codificador de 2 entradas e 4 saídas
  //   f3
  //   W
  //   Somador  de 4 bits
endmodule

module aaa (
  input  a,
  input  b,
  input  c,
  input  d,
  output cout,
  output s
);

  wire and_1_out, and_2_out, and_3_out, and_4_out, and_5_out, and_6_out;

  and and_1 (and_1_out, a, b);
  and and_2 (and_2_out, a, c);
  and and_3 (and_3_out, b, c);
  and and_4 (and_4_out, a, d);
  and and_5 (and_5_out, b, d);
  and and_6 (and_6_out, c, d);
  xor odd_parity_1 (s, a, b, c, d);
  or or_1 (cout, and_1_out, and_2_out, and_3_out, and_4_out, and_5_out, and_6_out);
endmodule
